# Fritzing sketch Arduino Nano DMX RS485 (saved by Fritzing 0.9.4)
breadboards: 1

parts:
  U1 = RS485 [package=so08]
  Bauteil1 = Arduino Nano (Rev3.0)
  XLR1 = XLR NC3MAAH [package=nc3maah]

nets:
  N1: U1.RO, Bauteil1.D0/RX
  GND: U1._RE, U1.DE, U1.GND, Bauteil1.GND, XLR1.1
  N2: U1.A, XLR1.3
  N3: U1.B, XLR1.2
  VCC: U1.VCC, Bauteil1.5V
